// Logisim project cpu.circ as structural Verilog: 3 circuits, main circuit main
module main (
  input  [31:0] INSTRUCTION,
  input  CLOCK,
  output [31:0] FETCH_ADDRESS,
  output [31:0] s0_Value,
  output [31:0] s1_Value,
  output [31:0] s2_Value,
  output [31:0] ra_Value,
  output [31:0] sp_Value,
  output [31:0] out_9,
  output [4:0] out_10,
  output [31:0] out_11,
  output [3:0] out_12
);

  wire ALUsrc, ExtOp, Jump, main_2_signed_overflow, main_3_p1, main_3_p2, main_3_p4, main_3_p10, MemtoReg,
       MemWrite, nPCsel, RegDst, RegWrite;
  wire [4:0] multiplexer_2_out;
  wire [31:0] adder_1_out, adder_2_out, bit_extender_1_out, bit_extender_2_out, bit_extender_3_out, busA,
       busB, main_3_p11, multiplexer_1_out, multiplexer_3_out, multiplexer_4_out;

  assign bit_extender_1_out = {{16{INSTRUCTION[15]}}, INSTRUCTION[15:0]};  // Bit_Extender bit_extender_1
  Adder #(.width(32)) adder_1 (.a(32'h4), .b(FETCH_ADDRESS), .out(adder_1_out));  // open: cin, cout
  Adder #(.width(32)) adder_2 (.a(adder_1_out), .b(bit_extender_1_out), .out(adder_2_out));  // open: cin, cout
  Multiplexer #(.width(32)) multiplexer_1 (
    .in0(adder_1_out), .in1(adder_2_out), .out(multiplexer_1_out), .sel(nPCsel));  // open: en
  Register #(.width(32)) PC (.D(multiplexer_1_out), .Q(FETCH_ADDRESS), .clk(CLOCK));  // open: en, clr
  Control control_1 (
    .in(INSTRUCTION), .RegDst(RegDst), .ALUSrc(ALUsrc), .MemtoReg(MemtoReg), .RegWrite(RegWrite),
    .MemWrite(MemWrite), .nPCsel(nPCsel), .Jump(Jump), .ExtOp(ExtOp), .ALUctr(out_12));
  Multiplexer #(.width(5)) multiplexer_2 (
    .in0(INSTRUCTION[15:11]), .in1(INSTRUCTION[20:16]), .out(multiplexer_2_out), .sel(RegDst));  // open: en
  regfile_main main_1 (
    .Read_Register_1(INSTRUCTION[20:16]), .Read_Register_2(INSTRUCTION[25:21]),
    .Write_Register(multiplexer_2_out), .Write_Data(out_11), .Write_Enable(RegWrite), .Clock(CLOCK),
    .Read_Data_1(busA), .Read_Data_2(busB), .s0_Value(s0_Value), .s1_Value(s1_Value), .s2_Value(s2_Value),
    .ra_Value(ra_Value), .sp_Value(sp_Value));
  assign bit_extender_2_out = {{16{1'b0}}, INSTRUCTION[15:0]};  // Bit_Extender bit_extender_2
  assign bit_extender_3_out = {{16{INSTRUCTION[15]}}, INSTRUCTION[15:0]};  // Bit_Extender bit_extender_3
  Multiplexer #(.width(32)) multiplexer_3 (
    .in0(bit_extender_2_out), .in1(bit_extender_3_out), .out(multiplexer_3_out), .sel(ExtOp));  // open: en
  alu_main main_2 (
    .Switch(out_12), .X(busA), .Result(out_9), .Signed_Overflow(main_2_signed_overflow), .Y(multiplexer_4_out));  // open: Equal
  Multiplexer #(.width(32)) multiplexer_4 (
    .in0(busB), .in1(multiplexer_3_out), .out(multiplexer_4_out), .sel(ALUsrc));  // open: en
  LED led_1 (.in(main_2_signed_overflow));
  // mem_main main_3: pin names not known; wires that end beside it: main_3_p1, main_3_p2, main_3_p2, main_3_p4, out_9, busB, MemWrite, main_3_p4, CLOCK, main_3_p10, main_3_p11
  Multiplexer #(.width(32)) multiplexer_5 (.in0(out_9), .in1(main_3_p11), .out(out_11), .sel(MemtoReg));  // open: en

  assign out_10 = INSTRUCTION[20:16];

  // Other names for the same wires on the sheet: ALUctr[3:0] = out_12; busW[31:0] = out_11; clk = CLOCK;
  //   fetch_addr[31:0] = FETCH_ADDRESS; imm[15:0] = INSTRUCTION[15:0]; rd[4:0] = INSTRUCTION[15:11];
  //   rt[4:0] = INSTRUCTION[20:16]; rs[4:0] = INSTRUCTION[25:21]; ra[31:0] = ra_Value; s0[31:0] = s0_Value;
  //   s1[31:0] = s1_Value; s2[31:0] = s2_Value; sp[31:0] = sp_Value

  // Notes on the sheet:
  //   Output
  //   These are outputs/inputs from run.circ
  //   Inputs
  //   These are DEBUG/TEST outputs from your circuit.
endmodule

module Control2 (
  input  [31:0] in,
  output [11:0] out_2,
  output out_3,
  output out_4,
  output out_5,
  output out_6,
  output out_7,
  output out_8,
  output out_9,
  output out_10,
  output [3:0] out_11
);

  wire undriven;
  wire [11:0] multiplexer_1_out, multiplexer_3_out, multiplexer_4_out, multiplexer_5_out;
  wire [31:0] shifter_1_out;

  Shifter #(.width(32)) shifter_1 (.in(in), .\dist (5'b11010), .out(shifter_1_out));
  Multiplexer #(.select(5), .width(12)) multiplexer_1 (
    .in0(12'h90), .in3(12'h290), .out(multiplexer_1_out), .sel(in[4:0]));  // open: in1, in2, in4, in5, in6, in7, in8, in9, in10, in11, in12, in13, in14, in15, in16, in17, in18, in19, in20, in21, in22, in23, in24, in25, in26, in27, in28, in29, in30, in31, en
  Multiplexer #(.width(12)) multiplexer_2 (
    .in0(multiplexer_1_out), .in1(multiplexer_3_out), .out(out_2), .sel(in[5]), .en(undriven));
  Multiplexer #(.select(5), .width(12)) multiplexer_3 (
    .in0(12'h590), .in1(12'h690), .in4(12'h990), .in5(12'ha90), .in10(12'hb90), .in11(12'hc90),
    .out(multiplexer_3_out), .sel(in[4:0]));  // open: in2, in3, in6, in7, in8, in9, in12, in13, in14, in15, in16, in17, in18, in19, in20, in21, in22, in23, in24, in25, in26, in27, in28, in29, in30, in31, en
  Multiplexer #(.select(5), .width(12)) multiplexer_4 (
    .in0(out_2), .in1(out_2), .out(multiplexer_4_out), .sel(shifter_1_out[4:0]));  // open: in2, in3, in4, in5, in6, in7, in8, in9, in10, in11, in12, in13, in14, in15, in16, in17, in18, in19, in20, in21, in22, in23, in24, in25, in26, in27, in28, in29, in30, in31, en
  Multiplexer #(.select(5), .width(12)) multiplexer_5 (
    .out(multiplexer_5_out), .sel(shifter_1_out[4:0]));  // open: in0, in1, in2, in3, in4, in5, in6, in7, in8, in9, in10, in11, in12, in13, in14, in15, in16, in17, in18, in19, in20, in21, in22, in23, in24, in25, in26, in27, in28, in29, in30, in31, en
  Multiplexer #(.width(12)) multiplexer_6 (
    .in0(multiplexer_4_out), .in1(multiplexer_5_out),
    .out({out_11, out_10, out_9, out_8, out_7, out_6, out_5, out_4, out_3}), .sel(shifter_1_out[5]));  // open: en
endmodule

module Control (
  input  [31:0] in,
  output RegDst,
  output ALUSrc,
  output MemtoReg,
  output RegWrite,
  output MemWrite,
  output nPCsel,
  output Jump,
  output ExtOp,
  output [3:0] ALUctr
);

  wire add, addi, addu, \and , \or , or_1_out, rtype, slt, sltu, sra, srl, sub, subu;
  wire [3:0] multiplexer_2_out, multiplexer_3_out, multiplexer_4_out, multiplexer_5_out, multiplexer_6_out,
       multiplexer_7_out, multiplexer_8_out, multiplexer_9_out, multiplexer_10_out;
  wire [5:0] funcO;

  Comparator #(.width(6), .mode("unsigned")) comparator_1 (.a(in[31:26]), .b({6{1'b0}}), .eq(rtype));  // open: gt, lt
  Comparator #(.width(6), .mode("unsigned")) comparator_2 (.a(in[31:26]), .b(6'b001000), .eq(addi));  // open: gt, lt
  Comparator #(.width(6), .mode("unsigned")) comparator_3 (.a(in[31:26]));  // open: b, gt, eq, lt
  Comparator #(.width(6), .mode("unsigned")) comparator_4 (.a(in[31:26]));  // open: b, gt, eq, lt
  Comparator #(.width(6), .mode("unsigned")) comparator_5 (.a(in[31:26]));  // open: b, gt, eq, lt
  Comparator #(.width(6), .mode("unsigned")) comparator_6 (.a(in[31:26]));  // open: b, gt, eq, lt
  Comparator #(.width(6), .mode("unsigned")) comparator_7 (.a(in[31:26]));  // open: b, gt, eq, lt
  Comparator #(.width(6), .mode("unsigned")) comparator_8 (.a(in[31:26]));  // open: b, gt, eq, lt
  Comparator #(.width(6), .mode("unsigned")) comparator_9 (.a(in[31:26]));  // open: b, gt, eq, lt
  Comparator #(.width(6), .mode("unsigned")) comparator_10 (.a(in[31:26]));  // open: b, gt, eq, lt
  Comparator #(.width(6), .mode("unsigned")) comparator_11 (.a(in[31:26]));  // open: b, gt, eq, lt
  Comparator #(.width(6), .mode("unsigned")) comparator_12 (.a(in[31:26]));  // open: b, gt, eq, lt
  Multiplexer #(.width(6)) multiplexer_1 (.in0({6{1'b1}}), .in1(in[5:0]), .out(funcO), .sel(rtype));  // open: en
  Comparator #(.width(6), .mode("unsigned")) comparator_13 (.a(funcO), .b(6'b100000), .eq(add));  // open: gt, lt
  Comparator #(.width(6), .mode("unsigned")) comparator_14 (.a(funcO), .b(6'b000010), .eq(srl));  // open: gt, lt
  Comparator #(.width(6), .mode("unsigned")) comparator_15 (.a(funcO), .b(6'b000011), .eq(sra));  // open: gt, lt
  Comparator #(.width(6), .mode("unsigned")) comparator_16 (.a(funcO), .b(6'b100001), .eq(addu));  // open: gt, lt
  Comparator #(.width(6), .mode("unsigned")) comparator_17 (.a(funcO), .b(6'b100010), .eq(sub));  // open: gt, lt
  Comparator #(.width(6), .mode("unsigned")) comparator_18 (.a(funcO), .b(6'b100011), .eq(subu));  // open: gt, lt
  Comparator #(.width(6), .mode("unsigned")) comparator_19 (.a(funcO), .b(6'b100100), .eq(\and ));  // open: gt, lt
  Comparator #(.width(6), .mode("unsigned")) comparator_20 (.a(funcO), .b(6'b100101), .eq(\or ));  // open: gt, lt
  Comparator #(.width(6), .mode("unsigned")) comparator_21 (.a(funcO), .b(6'b101010), .eq(slt));  // open: gt, lt
  Comparator #(.width(6), .mode("unsigned")) comparator_22 (.a(funcO), .b(6'b101011), .eq(sltu));  // open: gt, lt
  Multiplexer #(.width(4)) multiplexer_2 (
    .in0(4'b0000), .in1(4'b0001), .out(multiplexer_2_out), .sel(srl));  // open: en
  Multiplexer #(.width(4)) multiplexer_3 (
    .in0(multiplexer_2_out), .in1(4'b0010), .out(multiplexer_3_out), .sel(sra));  // open: en
  or or_1 (or_1_out, add, addi);
  Multiplexer #(.width(4)) multiplexer_4 (
    .in0(multiplexer_3_out), .in1(4'b0101), .out(multiplexer_4_out), .sel(or_1_out));  // open: en
  Multiplexer #(.width(4)) multiplexer_5 (
    .in0(multiplexer_4_out), .in1(4'b0110), .out(multiplexer_5_out), .sel(addu));  // open: en
  Multiplexer #(.width(4)) multiplexer_6 (
    .in0(multiplexer_5_out), .in1(4'b0111), .out(multiplexer_6_out), .sel(sub));  // open: en
  Multiplexer #(.width(4)) multiplexer_7 (
    .in0(multiplexer_6_out), .in1(4'b1000), .out(multiplexer_7_out), .sel(subu));  // open: en
  Multiplexer #(.width(4)) multiplexer_8 (
    .in0(multiplexer_7_out), .in1(4'b1001), .out(multiplexer_8_out), .sel(\and ));  // open: en
  Multiplexer #(.width(4)) multiplexer_9 (
    .in0(multiplexer_8_out), .in1(4'b1010), .out(multiplexer_9_out), .sel(\or ));  // open: en
  Multiplexer #(.width(4)) multiplexer_10 (
    .in0(multiplexer_9_out), .in1(4'b1011), .out(multiplexer_10_out), .sel(slt));  // open: en
  Multiplexer #(.width(4)) multiplexer_11 (
    .in0(multiplexer_10_out), .in1(4'b1100), .out(ALUctr), .sel(sltu));  // open: en
  or or_2 (RegWrite, rtype, addi);
  or or_3 (RegDst, rtype, addi);
  buf or_4 (ALUSrc, addi);  // OR_Gate
  buf or_5 (MemtoReg, 1'b0);  // OR_Gate
  buf or_6 (MemWrite, 1'b0);  // OR_Gate
  buf or_7 (nPCsel, 1'b0);  // OR_Gate
  buf or_8 (Jump, 1'b0);  // OR_Gate
  buf or_9 (ExtOp, addi);  // OR_Gate

  // Other names for the same wires on the sheet: func[5:0] = in[5:0]; opcode[5:0] = in[31:26]
endmodule
